# Fritzing sketch sketch (saved by Fritzing 0.9.3b)
breadboards: 1

parts:
  Part1 = Arduino Uno (Rev3)
  J1 = Basic Servo
  hc-sr1 = hc-sr04

nets:
  N1: Part1.D10_PWM/SS, J1.pulse
  N2: Part1.D7, hc-sr1.Trig, hc-sr1.Echo
  VCC: Part1.5V, J1.vcc, hc-sr1.VCC
  GND: Part1.GND, J1.gnd, hc-sr1.GND
