# Fritzing sketch sketch_task2 (saved by Fritzing 0.9.3b)
breadboards: 1

parts:
  Part1 = Arduino Uno (Rev3)
  S1 = Pushbutton [package="[THT]"]
  R1 = Resistor [tolerance=±5% resistance=220 package=THT]
  J1 = Piezo Speaker

nets:
  N1: Part1.GND, R1.Pin_1, J1.pin1
  N2: Part1.D4, S1.Pin_1, S1.Pin_2, R1.Pin_0
  N3: Part1.D6_PWM, J1.pin2
  N4: Part1.5V, S1.Pin_3, S1.Pin_4
